# Fritzing sketch flatbox-4LEDs (saved by Fritzing 0.9.3b)
breadboards: 1

parts:
  R1 = Resistor [tolerance=±5% resistance=1.5k package=THT]
  LED1 = LED - 5mm [color="White (6500K)" package="5 mm [THT]"]
  VCC1 = 4 x AAA Battery Mount
  R2 = Resistor [tolerance=±5% resistance=1.5k package=THT]
  LED2 = LED - 5mm [color="White (6500K)" package="5 mm [THT]"]
  R3 = Resistor [tolerance=±5% resistance=1.5k package=THT]
  LED3 = LED - 5mm [color="White (6500K)" package="5 mm [THT]"]
  R4 = Resistor [tolerance=±5% resistance=1.5k package=THT]
  LED4 = LED - 5mm [color="White (6500K)" package="5 mm [THT]"]
  R5 = Rotary Potentiometer (Small) [maximum_resistance=100kΩ package=THT]

nets:
  N1: R1.Pin_0, LED1.cathode
  N2: R1.Pin_1, R2.Pin_1, R3.Pin_1, R4.Pin_1, R5.leg2
  N3: LED1.anode, VCC1.+, LED2.anode, LED3.anode, LED4.anode
  N4: VCC1.-, R5.wiper
  N5: R2.Pin_0, LED2.cathode
  N6: R3.Pin_0, LED3.cathode
  N7: R4.Pin_0, LED4.cathode
